# Fritzing sketch 555 transistores REV2 (saved by Fritzing 0.9.10b)
circuit board: 10cm x 7.5cm
breadboards: 1

parts:
  Q5 = NPN-Transistor [part_number=C945 package="TO92 [THT]"]
  Q6 = NPN-Transistor [part_number=C945 package="TO92 [THT]"]
  Q7 = NPN-Transistor [part_number=C945 package="TO92 [THT]"]
  R1 = Resistor [tolerance=±5% resistance=4.7k power=0.25 package=THT]
  R2 = Resistor [tolerance=±5% resistance=820 power=0.25 package=THT]
  R3 = Resistor [tolerance=±5% resistance=4.7k power=0.25 package=THT]
  R4 = Resistor [tolerance=±5% resistance=10k power=0.25 package=THT]
  JP1 = Header 1 [part_number=Ground package=smtso-256-et]
  JP8 = Header 1 [part_number=Vcc package=smtso-256-et]
  JP5 = Header 1 [part_number=Control_Voltage package=smtso-256-et]
  R5 = Resistor [tolerance=±5% resistance=4.7k power=0.25 package=THT]
  R6 = Resistor [tolerance=±5% resistance=4.7k power=0.25 package=THT]
  R7 = Resistor [tolerance=±5% resistance=4.7k power=0.25 package=THT]
  Q9 = PNP-Transistor [part_number=A1015 package="TO92 [THT]"]
  Q10 = PNP-Transistor [part_number=A1015 package="TO92 [THT]"]
  Q11 = PNP-Transistor [part_number=A1015 package="TO92 [THT]"]
  Q12 = PNP-Transistor [part_number=A1015 package="TO92 [THT]"]
  Q13 = PNP-Transistor [part_number=A1015 package="TO92 [THT]"]
  R8 = Resistor [tolerance=±5% resistance=100k power=0.25 package=THT]
  JP2 = Header 1 [part_number=Trigger package=smtso-256-et]
  R9 = Resistor [tolerance=±5% resistance=1k power=0.25 package=THT]
  Q14 = PNP-Transistor [part_number=S9015 package="TO92 [THT]"]
  Q15 = PNP-Transistor [part_number=S9015 package="TO92 [THT]"]
  R10 = Resistor [tolerance=±5% resistance=4.7k power=0.25 package=THT]
  R11 = Resistor [tolerance=±5% resistance=15k power=0.25 package=THT]
  Q16 = NPN-Transistor [part_number=C945 package="TO92 [THT]"]
  R12 = Resistor [tolerance=±5% resistance=6.8k power=0.25 package=THT]
  R13 = Resistor [tolerance=±5% resistance=4.7k power=0.25 package=THT]
  Q17 = NPN-Transistor [part_number=C945 package="TO92 [THT]"]
  Q18 = NPN-Transistor [part_number=C945 package="TO92 [THT]"]
  Q19 = NPN-Transistor [part_number=C945 package="TO92 [THT]"]
  Q20 = NPN-Transistor [part_number=C945 package="TO92 [THT]"]
  Q21 = NPN-Transistor [part_number=C945 package="TO92 [THT]"]
  R14 = Resistor [tolerance=±5% resistance=3.9k power=0.25 package=THT]
  Q25 = PNP-Transistor [part_number=S9012 package="TO92 [THT]"]
  Q22 = NPN-Transistor [part_number=S8050 package="TO92 [THT]"]
  JP3 = Header 1 [part_number=Output package=smtso-256-et]
  Q23 = NPN-Transistor [part_number=S8050 package="TO92 [THT]"]
  R15 = Resistor [tolerance=±5% resistance=220 power=0.25 package=THT]
  R16 = Resistor [tolerance=±5% resistance=100k power=0.25 package=THT]
  JP4 = Header 1 [part_number=Reset package=smtso-256-et]
  Q26 = PNP-Transistor [part_number=A1015 package="TO92 [THT]"]
  R17 = Resistor [tolerance=±5% resistance=100 power=0.25 package=THT]
  Q24 = NPN-Transistor [part_number=S8050 package="TO92 [THT]"]
  JP7 = Header 1 [part_number=Discharge package=smtso-256-et]
  JP6 = Header 1 [part_number=Threshold package=smtso-256-et]
  Q8 = NPN-Transistor [part_number=C945 package="TO92 [THT]"]
  Q1 = PNP-Transistor [part_number=BC557 package="TO92 [THT]"]
  Q2 = PNP-Transistor [part_number=BC557 package="TO92 [THT]"]
  Q3 = PNP-Transistor [part_number=BC557 package="TO92 [THT]"]
  Q4 = PNP-Transistor [part_number=BC557 package="TO92 [THT]"]

nets:
  N1: Q5.E, Q6.B
  N2: Q5.B, JP6.1
  N3: Q5.C, Q6.C, Q1.B, Q1.C, Q2.B
  N4: Q6.E, R4.Pin_1, Q8.E
  N5: Q7.E, Q8.B
  N6: Q7.B, JP5.1, R5.Pin_0, R6.Pin_1
  N7: Q7.C, Q8.C, Q3.B, Q4.B, Q4.C
  N8: R1.Pin_0, Q1.E
  N9: R1.Pin_1, R2.Pin_1, R3.Pin_1, JP8.1, R5.Pin_1, R9.Pin_1, Q14.E, Q15.E, R12.Pin_1, Q21.C, Q22.C
  N10: R2.Pin_0, Q2.E, Q3.E
  N11: R3.Pin_0, Q4.E
  GND: R4.Pin_0, JP1.1, R7.Pin_0, Q12.C, Q13.C, R8.Pin_0, R13.Pin_0, Q18.E, Q19.E, Q20.E, Q23.E, Q24.E, Q3.C
  N12: R6.Pin_0, R7.Pin_1, Q13.B
  N13: Q9.E, R9.Pin_0
  N14: Q9.B, Q14.B, Q14.C, Q15.B, R11.Pin_1
  N15: Q9.C, Q11.E, Q12.E
  N16: Q10.E, Q11.B
  N17: Q10.B, JP2.1
  N18: Q10.C, Q11.C, R8.Pin_1, Q18.B
  N19: Q12.B, Q13.E
  N20: Q15.C, R10.Pin_1, Q16.B, Q20.C
  N21: R10.Pin_0, Q18.C, Q19.B, Q2.C
  N22: R11.Pin_0, Q17.B, Q17.C, Q26.E
  N23: Q16.E, R13.Pin_1, R15.Pin_0, R17.Pin_1
  N24: Q16.C, R12.Pin_0, Q21.B, Q25.B, Q25.C
  N25: Q17.E, Q19.C, Q20.B
  N26: Q21.E, R14.Pin_1, Q22.B
  N27: R14.Pin_0, Q25.E, Q22.E, JP3.1, Q23.C
  N28: Q23.B, R15.Pin_1
  N29: R16.Pin_0, Q26.B
  N30: R16.Pin_1, JP4.1
  N31: Q26.C, R17.Pin_0, Q24.B
  N32: Q24.C, JP7.1

notes:
  Discrete 555
  Threshold Comparator
  Voltage Divider
  Trigger Comparator
  Reset
  RS Flip-Flop
  Output Driver
